# Fritzing sketch seven-segment (saved by Fritzing 0.9.3b)
circuit board: 99.9cm x 99.9cm
breadboards: 1

parts:
  IC1 = PICAXE-18 [package=THT]
  IC2 = PICAXE-18 [package=THT]
  IC3 = PICAXE-18 [package=THT]
  IC4 = PICAXE-18 [package=THT]
  J1 = female pin header, 11 pins [form="♀ (female)"]
  J2 = female pin header, 10 pins [form="♀ (female)"]
  J3 = female pin header, 4 pins [form="♀ (female)"]
  J4 = female pin header, 15 pins [form="♀ (female)"]  # not connected
  R1 = Resistor [tolerance=±5% resistance=220 package="0603 [SMD]"]  # not connected
  R2 = Resistor [tolerance=±5% resistance=220 package="0603 [SMD]"]  # not connected
  R3 = Resistor [tolerance=±5% resistance=220 package="0603 [SMD]"]  # not connected
  R4 = Resistor [tolerance=±5% resistance=220 package="0603 [SMD]"]  # not connected
  R5 = Resistor [tolerance=±5% resistance=220 package="0603 [SMD]"]  # not connected
  R6 = Resistor [tolerance=±5% resistance=220 package="0603 [SMD]"]  # not connected
  R7 = Resistor [tolerance=±5% resistance=220 package="0603 [SMD]"]  # not connected
  R8 = Resistor [tolerance=±5% resistance=220 package="0603 [SMD]"]  # not connected
  R9 = Resistor [tolerance=±5% resistance=220 package="0603 [SMD]"]  # not connected
  R10 = Resistor [tolerance=±5% resistance=220 package="0603 [SMD]"]  # not connected
  R11 = Resistor [tolerance=±5% resistance=220 package="0603 [SMD]"]  # not connected
  R12 = Resistor [tolerance=±5% resistance=220 package="0603 [SMD]"]  # not connected
  R13 = Resistor [tolerance=±5% resistance=220 package="0603 [SMD]"]  # not connected
  R14 = Resistor [tolerance=±5% resistance=220 package="0603 [SMD]"]  # not connected
  R15 = Resistor [tolerance=±5% resistance=220 package="0603 [SMD]"]  # not connected
  IC5 = PICAXE-18 [package=THT]
  R16 = Resistor [tolerance=±5% resistance=220 package="0603 [SMD]"]  # not connected
  R17 = Resistor [tolerance=±5% resistance=220 package="0603 [SMD]"]  # not connected
  R18 = Resistor [tolerance=±5% resistance=220 package="0603 [SMD]"]  # not connected
  R19 = Resistor [tolerance=±5% resistance=220 package="0603 [SMD]"]  # not connected
  D1 = LTE-302 [package=lte-302]
  D2 = LTE-302 [package=lte-302]

nets:
  N1: IC1.+V, IC3.+V, J2.pin10, J3.pin2, D1.C
  N2: IC1.In_6, IC3.In_6, J1.pin11, J3.pin1
  N3: IC2.+V, IC4.+V, J2.pin9, J3.pin4
  N4: IC2.In_6, IC4.In_6, J1.pin10, J3.pin3, D2.C
  N5: IC3.Out_6, IC3.In_0, IC4.Out_6, IC4.In_0, J2.pin8
  N6: J1.pin9, IC5.In_2
