# Fritzing sketch led_arduino_fritzing_continue_2 (saved by Fritzing 0.9.2b)
perfboards: 1
breadboards: 1

parts:
  Power_plug5 = Power plug
  C9 = Electrolytic Capacitor [capacitance=100µF voltage=12V package="100 mil [THT, electrolytic]"]
  IC4 = ULN2003A [package="DIP16 [THT]"]
  C10 = Electrolytic Capacitor [capacitance=100µF voltage=12V package="100 mil [THT, electrolytic]"]
  U7 = atmega328 [package=dip]
  J3 = female pin header, 6 pins [form="♀ (female)"]
  LED9 = RGB LED (com. anode, rbg) [package="5 mm [THT]"]
  LED10 = RGB LED - (4 legs) [package="5 mm [THT]"]
  R5 = Resistor [tolerance=±5% resistance=1k package=THT]
  R6 = Resistor [tolerance=±1% resistance=2k package=THT]
  Q25 = Basic FET N-Channel [package="TO220 [THT]"]
  Q26 = Basic FET N-Channel [package="TO220 [THT]"]
  Q27 = Basic FET N-Channel [package="TO220 [THT]"]
  Q28 = Basic FET N-Channel [package="TO220 [THT]"]
  Q29 = Basic FET N-Channel [package="TO220 [THT]"]
  Q30 = Basic FET N-Channel [package="TO220 [THT]"]
  IC5 = ULN2003A [package="DIP16 [THT]"]
  U8 = atmega328 [package=dip]
  Power_plug6 = Power plug
  C11 = Electrolytic Capacitor [capacitance=100µF voltage=12V package="100 mil [THT, electrolytic]"]
  C12 = Electrolytic Capacitor [capacitance=100µF voltage=12V package="100 mil [THT, electrolytic]"]
  R7 = Resistor [tolerance=±1% resistance=2k package=THT]
  R8 = Resistor [tolerance=±5% resistance=1k package=THT]
  J4 = female pin header, 6 pins [form="♀ (female)"]
  Q31 = Basic FET N-Channel [package="TO220 [THT]"]
  Q32 = Basic FET N-Channel [package="TO220 [THT]"]
  Q33 = Basic FET N-Channel [package="TO220 [THT]"]

nets:
  N1: Power_plug5.GND, C9.-, IC4.In_5, IC4.COM_-_Common, IC4.Out_5, IC4.Out_4, C10.-, R6.Pin_0
  N2: Power_plug5.VCC, C9.+, IC4.Out_1, LED9.common_anode, LED10.common_anode
  N3: IC4.In_3, IC4.In_7, C10.+, U7.VCC, U7.AVCC, J3.pin2
  N4: U7.D0_(RX), J3.pin4
  N5: U7.D1_(TX), R5.Pin_1
  N6: U7.D3_(PWM), Q26.gate
  N7: U7.D5_(PWM), Q25.gate
  N8: U7.D6_(PWM), Q27.gate
  N9: U7.D9_(PWM), Q29.gate
  N10: U7.D10_(PWM), Q28.gate
  N11: U7.D11_(PWM), Q30.gate
  N12: U7.GND#21, Q28.source
  N13: J3.pin5, R6.Pin_1
  N14: IC5.In_3, IC5.In_7, U8.VCC, U8.AVCC, C12.-, J4.pin5
  GND: IC5.In_5, IC5.COM_-_Common, IC5.Out_5, IC5.Out_4, U8.GND, Power_plug6.GND, C11.+, C12.+, R7.Pin_0, J4.pin4, Q31.source, Q32.source, Q33.source
  N15: IC5.Out_1, Power_plug6.VCC, C11.-
  N16: U8.D0_(RX), J4.pin3
  N17: U8.D1_(TX), R8.Pin_1
  N18: U8.D9_(PWM), Q33.gate
  N19: U8.D10_(PWM), Q31.gate
  N20: U8.D11_(PWM), Q32.gate
  N21: R7.Pin_1, R8.Pin_0, J4.pin2
